// Digital circuit 1X18 RAM.dig as structural Verilog
module _1X18_RAM (
  input  RS1,
  input  RS2,
  input  WS,
  input  [17:0] WD_17_0,
  input  CLK,
  output [17:0] RD1_17_0,
  output [17:0] RD2_17_0
);

  _1X1_RAM _1x1_ram_1 (.RS1(RS1), .RS2(RS2), .WD(WD_17_0[0]), .WS(WS), .CLK(CLK), .RD1(RD1_17_0[0]), .RD2(RD2_17_0[0]));
  _1X1_RAM _1x1_ram_2 (.RS1(RS1), .RS2(RS2), .WD(WD_17_0[6]), .WS(WS), .CLK(CLK), .RD1(RD1_17_0[6]), .RD2(RD2_17_0[6]));
  _1X1_RAM _1x1_ram_3 (
    .RS1(RS1), .RS2(RS2), .WD(WD_17_0[12]), .WS(WS), .CLK(CLK), .RD1(RD1_17_0[12]), .RD2(RD2_17_0[12]));
  _1X1_RAM _1x1_ram_4 (.RS1(RS1), .RS2(RS2), .WD(WD_17_0[1]), .WS(WS), .CLK(CLK), .RD1(RD1_17_0[1]), .RD2(RD2_17_0[1]));
  _1X1_RAM _1x1_ram_5 (.RS1(RS1), .RS2(RS2), .WD(WD_17_0[7]), .WS(WS), .CLK(CLK), .RD1(RD1_17_0[7]), .RD2(RD2_17_0[7]));
  _1X1_RAM _1x1_ram_6 (
    .RS1(RS1), .RS2(RS2), .WD(WD_17_0[13]), .WS(WS), .CLK(CLK), .RD1(RD1_17_0[13]), .RD2(RD2_17_0[13]));
  _1X1_RAM _1x1_ram_7 (.RS1(RS1), .RS2(RS2), .WD(WD_17_0[2]), .WS(WS), .CLK(CLK), .RD1(RD1_17_0[2]), .RD2(RD2_17_0[2]));
  _1X1_RAM _1x1_ram_8 (.RS1(RS1), .RS2(RS2), .WD(WD_17_0[8]), .WS(WS), .CLK(CLK), .RD1(RD1_17_0[8]), .RD2(RD2_17_0[8]));
  _1X1_RAM _1x1_ram_9 (
    .RS1(RS1), .RS2(RS2), .WD(WD_17_0[14]), .WS(WS), .CLK(CLK), .RD1(RD1_17_0[14]), .RD2(RD2_17_0[14]));
  _1X1_RAM _1x1_ram_10 (
    .RS1(RS1), .RS2(RS2), .WD(WD_17_0[3]), .WS(WS), .CLK(CLK), .RD1(RD1_17_0[3]), .RD2(RD2_17_0[3]));
  _1X1_RAM _1x1_ram_11 (
    .RS1(RS1), .RS2(RS2), .WD(WD_17_0[9]), .WS(WS), .CLK(CLK), .RD1(RD1_17_0[9]), .RD2(RD2_17_0[9]));
  _1X1_RAM _1x1_ram_12 (
    .RS1(RS1), .RS2(RS2), .WD(WD_17_0[15]), .WS(WS), .CLK(CLK), .RD1(RD1_17_0[15]), .RD2(RD2_17_0[15]));
  _1X1_RAM _1x1_ram_13 (
    .RS1(RS1), .RS2(RS2), .WD(WD_17_0[4]), .WS(WS), .CLK(CLK), .RD1(RD1_17_0[4]), .RD2(RD2_17_0[4]));
  _1X1_RAM _1x1_ram_14 (
    .RS1(RS1), .RS2(RS2), .WD(WD_17_0[10]), .WS(WS), .CLK(CLK), .RD1(RD1_17_0[10]), .RD2(RD2_17_0[10]));
  _1X1_RAM _1x1_ram_15 (
    .RS1(RS1), .RS2(RS2), .WD(WD_17_0[16]), .WS(WS), .CLK(CLK), .RD1(RD1_17_0[16]), .RD2(RD2_17_0[16]));
  _1X1_RAM _1x1_ram_16 (
    .RS1(RS1), .RS2(RS2), .WD(WD_17_0[5]), .WS(WS), .CLK(CLK), .RD1(RD1_17_0[5]), .RD2(RD2_17_0[5]));
  _1X1_RAM _1x1_ram_17 (
    .RS1(RS1), .RS2(RS2), .WD(WD_17_0[11]), .WS(WS), .CLK(CLK), .RD1(RD1_17_0[11]), .RD2(RD2_17_0[11]));
  _1X1_RAM _1x1_ram_18 (
    .RS1(RS1), .RS2(RS2), .WD(WD_17_0[17]), .WS(WS), .CLK(CLK), .RD1(RD1_17_0[17]), .RD2(RD2_17_0[17]));

  // Other names for the same wires on the sheet: RD1_0 = RD1_17_0[0]; RD1_1 = RD1_17_0[1]; RD1_2 = RD1_17_0[2];
  //   RD1_3 = RD1_17_0[3]; RD1_4 = RD1_17_0[4]; RD1_5 = RD1_17_0[5]; RD1_6 = RD1_17_0[6]; RD1_7 = RD1_17_0[7];
  //   RD1_8 = RD1_17_0[8]; RD1_9 = RD1_17_0[9]; RD1_10 = RD1_17_0[10]; RD1_11 = RD1_17_0[11]; RD1_12 = RD1_17_0[12];
  //   RD1_13 = RD1_17_0[13]; RD1_14 = RD1_17_0[14]; RD1_15 = RD1_17_0[15]; RD1_16 = RD1_17_0[16];
  //   RD1_17 = RD1_17_0[17]; RD2_0 = RD2_17_0[0]; RD2_1 = RD2_17_0[1]; RD2_2 = RD2_17_0[2]; RD2_3 = RD2_17_0[3];
  //   RD2_4 = RD2_17_0[4]; RD2_5 = RD2_17_0[5]; RD2_6 = RD2_17_0[6]; RD2_7 = RD2_17_0[7]; RD2_8 = RD2_17_0[8];
  //   RD2_9 = RD2_17_0[9]; RD2_10 = RD2_17_0[10]; RD2_11 = RD2_17_0[11]; RD2_12 = RD2_17_0[12]; RD2_13 = RD2_17_0[13];
  //   RD2_14 = RD2_17_0[14]; RD2_15 = RD2_17_0[15]; RD2_16 = RD2_17_0[16]; RD2_17 = RD2_17_0[17]; WD0 = WD_17_0[0];
  //   WD1 = WD_17_0[1]; WD2 = WD_17_0[2]; WD3 = WD_17_0[3]; WD4 = WD_17_0[4]; WD5 = WD_17_0[5]; WD6 = WD_17_0[6];
  //   WD7 = WD_17_0[7]; WD8 = WD_17_0[8]; WD9 = WD_17_0[9]; WD10 = WD_17_0[10]; WD11 = WD_17_0[11];
  //   WD12 = WD_17_0[12]; WD13 = WD_17_0[13]; WD14 = WD_17_0[14]; WD15 = WD_17_0[15]; WD16 = WD_17_0[16];
  //   WD17 = WD_17_0[17]

  // Notes on the sheet:
  //   Fig:1X18 RAM
endmodule
