// Digital circuit 6 bit Not.dig as structural Verilog
module _6_bit_Not (
  input  [5:0] A_5_0,
  output [5:0] R_5_0
);

  not not_1 (R_5_0[0], A_5_0[0]);
  not not_2 (R_5_0[1], A_5_0[1]);
  not not_3 (R_5_0[2], A_5_0[2]);
  not not_4 (R_5_0[3], A_5_0[3]);
  not not_5 (R_5_0[4], A_5_0[4]);
  not not_6 (R_5_0[5], A_5_0[5]);

  // Notes on the sheet:
  //   Figure:6 bit Not Gate
endmodule
