// Digital circuit 6 bit Register Set.dig as structural Verilog
module _6_bit_Register_Set (
  input  [2:0] WR_2_0,
  input  WE,
  input  CLK,
  input  [2:0] RA_2_0,
  input  [2:0] RB_2_0,
  input  [5:0] WRD_5_0,
  output [5:0] B_5_0,
  output [5:0] A_5_0
);

  wire A0, A1, A2, A3, A4, A5, D0, D1, D2, D3, D4, D5, decoder_1_out_6;
  wire [5:0] R0, R1, R2, R3, R4, R5;

  and and_1 (D0, A0, WE);
  and and_2 (D1, A1, WE);
  and and_3 (D4, A4, WE);
  and and_4 (D2, A2, WE);
  and and_5 (D3, A3, WE);
  and and_6 (D5, A5, WE);
  Decoder #(.Selector_Bits(3)) decoder_1 (
    .sel(WR_2_0), .out_0(A0), .out_1(A1), .out_2(A2), .out_3(A3), .out_4(A4), .out_5(A5),
    .out_6(decoder_1_out_6), .out_7(decoder_1_out_6));
  _6_bit_Reg _6_bit_reg_1 (.Din_5_0(WRD_5_0), .Sel(D5), .CLK(CLK), .Dout_5_0(R5));
  _6_bit_Reg _6_bit_reg_2 (.Din_5_0(WRD_5_0), .Sel(D4), .CLK(CLK), .Dout_5_0(R4));
  _6_bit_Reg _6_bit_reg_3 (.Din_5_0(WRD_5_0), .Sel(D3), .CLK(CLK), .Dout_5_0(R3));
  _6_bit_Reg _6_bit_reg_4 (.Din_5_0(WRD_5_0), .Sel(D2), .CLK(CLK), .Dout_5_0(R2));
  _6_bit_Reg _6_bit_reg_5 (.Din_5_0(WRD_5_0), .Sel(D1), .CLK(CLK), .Dout_5_0(R1));
  _6_bit_Reg _6_bit_reg_6 (.Din_5_0(WRD_5_0), .Sel(D0), .CLK(CLK), .Dout_5_0(R0));
  Multiplexer #(.Selector_Bits(3), .Bits(6)) multiplexer_1 (
    .sel(RA_2_0), .in_0(R0), .in_1(R1), .in_2(R2), .in_3(R3), .in_4(R4), .in_5(R5), .in_6({6{1'b0}}),
    .in_7({6{1'b0}}), .out(A_5_0));
  Multiplexer #(.Selector_Bits(3), .Bits(6)) multiplexer_2 (
    .sel(RB_2_0), .in_0(R0), .in_1(R1), .in_2(R2), .in_3(R3), .in_4(R4), .in_5(R5), .in_6({6{1'b0}}),
    .in_7({6{1'b0}}), .out(B_5_0));
  // also tied to GND on the sheet: decoder_1_out_6

  // Other names for the same wires on the sheet: A[5:0] = A_5_0; B[5:0] = B_5_0; RA[2:0] = RA_2_0; RB[2:0] = RB_2_0;
  //   WRD[5:0] = WRD_5_0

  // Notes on the sheet:
  //   Fig:6 bit Register Set
endmodule
