// Digital circuit 1 bit Reg.dig as structural Verilog
module _1_bit_Reg (
  input  CLK,
  input  Din,
  input  Sel,
  output Dout
);

  wire multiplexer_1_out;

  Multiplexer multiplexer_1 (.sel(Sel), .in_0(Dout), .in_1(Din), .out(multiplexer_1_out));
  D_FF d_ff_1 (.D(multiplexer_1_out), .C(CLK), .Q(Dout));  // open: nQ

  // Notes on the sheet:
  //   Fig:1bit Register
endmodule
