// Digital circuit 3bit Program Counter.dig as structural Verilog
module _3bit_Program_Counter (
  input  CLK,
  input  [2:0] I_2_0,
  output [2:0] O_2_0
);

  _1_bit_Reg _1_bit_reg_1 (.Din(I_2_0[2]), .Sel(1'b1), .CLK(CLK), .Dout(O_2_0[2]));
  _1_bit_Reg _1_bit_reg_2 (.Din(I_2_0[1]), .Sel(1'b1), .CLK(CLK), .Dout(O_2_0[1]));
  _1_bit_Reg _1_bit_reg_3 (.Din(I_2_0[0]), .Sel(1'b1), .CLK(CLK), .Dout(O_2_0[0]));

  // Other names for the same wires on the sheet: B0 = O_2_0[0]; B1 = O_2_0[1]; B2 = O_2_0[2]; A0 = I_2_0[0];
  //   A1 = I_2_0[1]; A2 = I_2_0[2]

  // Notes on the sheet:
  //   Fig: 3bit Program Counter
endmodule
