// Digital circuit 6 bit ALU.dig as structural Verilog
module _6_bit_ALU (
  input  [1:0] OP_1_0,
  input  [5:0] A_5_0,
  input  [5:0] B_5_0,
  output [5:0] R_5_0
);

  wire [5:0] _6_bit_adder_1_r_5_0, _6_bit_not_1_r_5_0, _6_bit_shl_1_r_5_0;

  _6_bit_Adder _6_bit_adder_1 (.A_5_0(A_5_0), .B_5_0(B_5_0), .R_5_0(_6_bit_adder_1_r_5_0));  // open: Cout
  _6_bit_Not _6_bit_not_1 (.A_5_0(A_5_0), .R_5_0(_6_bit_not_1_r_5_0));
  _6_bit_SHL _6_bit_shl_1 (.A_5_0(A_5_0), .B_2_0(B_5_0), .R_5_0(_6_bit_shl_1_r_5_0));
  Multiplexer #(.Selector_Bits(2), .Bits(6)) multiplexer_1 (
    .sel(OP_1_0), .in_0(_6_bit_adder_1_r_5_0), .in_1(_6_bit_not_1_r_5_0), .in_2(_6_bit_shl_1_r_5_0),
    .in_3({6{1'b0}}), .out(R_5_0));

  // Other names for the same wires on the sheet: A[5:0] = A_5_0; B[5:0] = B_5_0

  // Notes on the sheet:
  //   Figure:6 bit ALU
endmodule
