// Digital circuit 6 bit Adder.dig as structural Verilog
module _6_bit_Adder (
  input  [5:0] A_5_0,
  input  [5:0] B_5_0,
  output Cout,
  output [5:0] R_5_0
);

  wire fa_2_cout, fa_3_cout, fa_4_cout, fa_5_cout, fa_6_cout;

  FA fa_1 (.X(A_5_0[5]), .Y(B_5_0[5]), .Cin(fa_2_cout), .S(R_5_0[5]), .Cout(Cout));
  FA fa_2 (.X(A_5_0[4]), .Y(B_5_0[4]), .Cin(fa_3_cout), .S(R_5_0[4]), .Cout(fa_2_cout));
  FA fa_3 (.X(A_5_0[3]), .Y(B_5_0[3]), .Cin(fa_4_cout), .S(R_5_0[3]), .Cout(fa_3_cout));
  FA fa_4 (.X(A_5_0[2]), .Y(B_5_0[2]), .Cin(fa_5_cout), .S(R_5_0[2]), .Cout(fa_4_cout));
  FA fa_5 (.X(A_5_0[1]), .Y(B_5_0[1]), .Cin(fa_6_cout), .S(R_5_0[1]), .Cout(fa_5_cout));
  FA fa_6 (.X(A_5_0[0]), .Y(B_5_0[0]), .Cin(1'b0), .S(R_5_0[0]), .Cout(fa_6_cout));

  // Notes on the sheet:
  //   Figure:6 bit Adder
endmodule
