// Digital circuit 6 bit Reg.dig as structural Verilog
module _6_bit_Reg (
  input  [5:0] Din_5_0,
  input  Sel,
  input  CLK,
  output [5:0] Dout_5_0
);

  _1_bit_Reg _1_bit_reg_1 (.Din(Din_5_0[5]), .Sel(Sel), .CLK(CLK), .Dout(Dout_5_0[5]));
  _1_bit_Reg _1_bit_reg_2 (.Din(Din_5_0[4]), .Sel(Sel), .CLK(CLK), .Dout(Dout_5_0[4]));
  _1_bit_Reg _1_bit_reg_3 (.Din(Din_5_0[3]), .Sel(Sel), .CLK(CLK), .Dout(Dout_5_0[3]));
  _1_bit_Reg _1_bit_reg_4 (.Din(Din_5_0[2]), .Sel(Sel), .CLK(CLK), .Dout(Dout_5_0[2]));
  _1_bit_Reg _1_bit_reg_5 (.Din(Din_5_0[1]), .Sel(Sel), .CLK(CLK), .Dout(Dout_5_0[1]));
  _1_bit_Reg _1_bit_reg_6 (.Din(Din_5_0[0]), .Sel(Sel), .CLK(CLK), .Dout(Dout_5_0[0]));

  // Other names for the same wires on the sheet: B0 = Dout_5_0[0]; B1 = Dout_5_0[1]; B2 = Dout_5_0[2];
  //   B3 = Dout_5_0[3]; B4 = Dout_5_0[4]; B5 = Dout_5_0[5]; A0 = Din_5_0[0]; A1 = Din_5_0[1]; A2 = Din_5_0[2];
  //   A3 = Din_5_0[3]; A4 = Din_5_0[4]; A5 = Din_5_0[5]

  // Notes on the sheet:
  //   Fig:6bit Register
endmodule
