// Digital circuit 6bit CU.dig as structural Verilog
module _6bit_CU (
  input  [3:0] Opcode_3_0,
  input  SF,
  input  ZF,
  output [1:0] Op_1_0,
  output REG_EN,
  output Imm_Sel,
  output JMP_Sel
);

  wire and_1_out, and_2_out, and_3_out, and_5_out, or_1_out;

  and and_1 (and_1_out, ~Opcode_3_0[0], ~Opcode_3_0[1]);  // And
  and and_2 (and_2_out, Opcode_3_0[0], ~Opcode_3_0[1], SF, ~ZF);  // And
  and and_3 (and_3_out, ~Opcode_3_0[2], ~Opcode_3_0[3]);  // And
  and and_4 (Imm_Sel, Opcode_3_0[2], ~Opcode_3_0[3]);  // And
  and and_5 (and_5_out, ~Opcode_3_0[2], Opcode_3_0[3]);  // And
  or or_1 (or_1_out, and_1_out, and_2_out);
  or or_2 (REG_EN, and_3_out, Imm_Sel);
  and and_6 (JMP_Sel, and_5_out, or_1_out);

  assign Op_1_0 = Opcode_3_0[1:0];

  // Notes on the sheet:
  //   Figure:6 bit CU
endmodule
