// Digital circuit CPU_Design.dig as structural Verilog
module CPU_Design (
  input  [2:0] WR_2_0,
  input  WE,
  input  [17:0] WD_17_0,
  input  CLK,
  input  PC_EN,
  input  [2:0] RA2_2_0,
  input  SF,
  input  ZF,
  output [17:0] RD2_17_0,
  output [2:0] R2_2_0,
  output [2:0] R1_2_0,
  output [2:0] WR_2_0_2,
  output [5:0] A_5_0,
  output [5:0] B_5_0,
  output [5:0] R_5_0,
  output [2:0] JMP_ADDR_2_0
);

  wire CPU_CLK, Imm_Sel, JMP_Sel, REG_EN;
  wire [1:0] Op;
  wire [2:0] _3bit_pc_adder_1_o_2_0, _3bit_program_counter_1_o_2_0, multiplexer_1_out;
  wire [5:0] _6_bit_register_set_1_b_5_0;
  wire [7:0] Don_t_Care;
  wire [17:14] _8x18_ram_1_rd1_17_0;

  Multiplexer #(.Bits(3)) multiplexer_1 (
    .sel(JMP_Sel), .in_0(_3bit_pc_adder_1_o_2_0), .in_1(JMP_ADDR_2_0), .out(multiplexer_1_out));
  _3bit_PC_Adder _3bit_pc_adder_1 (.I_2_0(_3bit_program_counter_1_o_2_0), .O_2_0(_3bit_pc_adder_1_o_2_0));
  _3bit_Program_Counter _3bit_program_counter_1 (
    .CLK(CPU_CLK), .I_2_0(multiplexer_1_out), .O_2_0(_3bit_program_counter_1_o_2_0));
  and and_1 (CPU_CLK, PC_EN, CLK);
  _8X18_RAM _8x18_ram_1 (
    .WD_17_0(WD_17_0), .WR_2_0(WR_2_0), .WE(WE), .CLK(CLK), .RA1_2_0(_3bit_program_counter_1_o_2_0),
    .RA2_2_0(RA2_2_0), .RD1_17_0({_8x18_ram_1_rd1_17_0, JMP_ADDR_2_0, R2_2_0, Don_t_Care}),
    .RD2_17_0(RD2_17_0));
  _6_bit_Register_Set _6_bit_register_set_1 (
    .WR_2_0(JMP_ADDR_2_0), .CLK(CPU_CLK), .WRD_5_0(R_5_0), .WE(REG_EN), .A_5_0(A_5_0),
    .B_5_0(_6_bit_register_set_1_b_5_0), .RA_2_0(JMP_ADDR_2_0), .RB_2_0(R2_2_0));
  _6_bit_ALU _6_bit_alu_1 (.R_5_0(R_5_0), .OP_1_0(Op), .A_5_0(A_5_0), .B_5_0(B_5_0));
  _6bit_CU _6bit_cu_1 (
    .Opcode_3_0(_8x18_ram_1_rd1_17_0), .SF(SF), .ZF(ZF), .Op_1_0(Op), .REG_EN(REG_EN), .Imm_Sel(Imm_Sel),
    .JMP_Sel(JMP_Sel));
  Multiplexer #(.Bits(6)) multiplexer_2 (
    .sel(Imm_Sel), .in_0(_6_bit_register_set_1_b_5_0), .in_1({R2_2_0, Don_t_Care[7:5]}), .out(B_5_0));

  assign R1_2_0 = JMP_ADDR_2_0;
  assign WR_2_0_2 = JMP_ADDR_2_0;

  // Other names for the same wires on the sheet: R2[2:0] = R2_2_0; JMP_ADDR[2:0] = JMP_ADDR_2_0;
  //   R1[2:0] = JMP_ADDR_2_0; A[5:0] = A_5_0; B[5:0] = B_5_0; R[5:0] = R_5_0

  // Notes on the sheet:
  //   Register Mode(00)=2bit(Type of op)+2bit(Op)+3bit(Reg1)+3bit(Reg2)+8bit(Don't care)
  //   Immediate Mode(01)=2bit(Type of op)+2bit(Op)+3bit(Reg1)+6bit(Imm Value)+5bit(Don't care)
  //   JMP Mode Mode(01)=2bit(Type of op)+2bit(Op)+3bit(Address)+11bit(Don't care)
  //   Add(Op=00),Not(Op=01),Shift Left(Op=10)
  //   JMP(Op=00),JL(Op=01)
  //                   JL START -> 10 01 010 00000000000
  //   START: SHL R1,R2    ->00 10 001 010 00000000
  //   JMP_TO: Add R1,5       -> 01 00 001 000101 00000
  //                  JMP JMP_TO  -> 10 00 010 00000000000
endmodule
